# Fritzing sketch schaltplan (saved by Fritzing 0.9.3b)
breadboards: 1

parts:
  Raspberry_Pi_1 = Raspberry Pi 3 [part_number=RPI-3-V1.2]
  S1 = H-Bridge with L298N
  VCC1 = Battery block 9V
  hc-sr1 = hc-sr04
  hc-sr2 = hc-sr04
  M1 = Stepper Motor - Bipolar
  R1 = Resistor [tolerance=±5% resistance=220 package="0402 [SMD]"]
  R2 = Resistor [tolerance=±5% resistance=220 package="0402 [SMD]"]
  R3 = Resistor [tolerance=±5% resistance=220 package="0402 [SMD]"]
  R4 = Resistor [tolerance=±5% resistance=220 package="0402 [SMD]"]

nets:
  GND: Raspberry_Pi_1.GND, S1.GND, S1.IN3, VCC1.-, hc-sr1.GND, hc-sr2.GND, R2.Pin_1, R3.Pin_1
  N1: Raspberry_Pi_1.GIPO17, S1.IN1
  N2: Raspberry_Pi_1.GIPO27, S1.IN2
  N3: Raspberry_Pi_1.GIPO19, R1.Pin_1, R2.Pin_0
  N4: Raspberry_Pi_1.GIPO26, hc-sr2.Trig
  N5: Raspberry_Pi_1.GIPO21, R3.Pin_0, R4.Pin_1
  N6: Raspberry_Pi_1.GIPO20, hc-sr1.Trig
  N7: Raspberry_Pi_1.GIPO23, S1.IN4
  VCC: Raspberry_Pi_1.5V, hc-sr1.VCC, hc-sr2.VCC
  N8: S1.12V, VCC1.+
  N9: S1.OUT4-Motor2, M1.B
  N10: hc-sr1.Echo, R4.Pin_0
  N11: hc-sr2.Echo, R1.Pin_0

custom parts:
  H-Bridge with L298N: h-bridge
